// Digital circuit spi-core.dig as structural Verilog
module spi_core (
  input  D0,
  input  CLK,
  input  SER_IN,
  input  D1,
  input  D2,
  input  D3,
  input  D4,
  input  D5,
  input  D6,
  input  D7,
  input  RD,
  input  WR,
  input  RESET,
  input  enable,
  output D0_2,
  output SER_OUT,
  output D1_2,
  output D2_2,
  output D3_2,
  output D4_2,
  output D5_2,
  output D6_2,
  output D7_2,
  output SCK
);

  wire _74161_1_pin11, _74161_1_pin12, _74161_1_pin13, _74161_1_pin14, _74299_1_pin11, and_1_out, and_2_out,
       count_clk, count_reset, nand_1_out, nand_2_out, nand_3_out, nand_4_out, not_2_out, shift, swr_t, t0,
       t1, t2, t3, t4, t5, t6, t7, t8, t9;

  and and_1 (and_1_out, CLK, enable);
  not not_1 (swr_t, WR);
  // ScopeTrigger #(.maxStepCount(30)) scopetrigger_1: pin names not known; wires that end beside it: and_1_out
  assign D0_2 = ~WR ? D0 : 1'bz;  // DriverInvSel driverinvsel_1
  assign D1_2 = ~WR ? D1 : 1'bz;  // DriverInvSel driverinvsel_2
  assign D2_2 = ~WR ? D2 : 1'bz;  // DriverInvSel driverinvsel_3
  assign D3_2 = ~WR ? D3 : 1'bz;  // DriverInvSel driverinvsel_4
  assign D4_2 = ~WR ? D4 : 1'bz;  // DriverInvSel driverinvsel_5
  assign D5_2 = ~WR ? D5 : 1'bz;  // DriverInvSel driverinvsel_6
  assign D6_2 = ~WR ? D6 : 1'bz;  // DriverInvSel driverinvsel_7
  assign D7_2 = ~WR ? D7 : 1'bz;  // DriverInvSel driverinvsel_8
  and and_2 (and_2_out, t9, RESET);
  nand nand_1 (nand_1_out, WR, nand_2_out);
  nand nand_2 (nand_2_out, nand_1_out, and_2_out);
  nand nand_3 (nand_3_out, t1, nand_4_out);
  nand nand_4 (nand_4_out, nand_3_out, and_2_out);
  not not_2 (not_2_out, nand_2_out);
  and and_3 (count_reset, WR, RESET);
  and and_4 (count_clk, CLK, not_2_out);
  nor nor_1 (SCK, CLK, nand_4_out);
  nand nand_5 (shift, nand_4_out, WR);
  _74299 _74299_1 (
    .pin1(shift), .pin2(RD), .pin3(RD), .pin4(D6_2), .pin5(D4_2), .pin6(D2_2), .pin7(D0_2), .pin9(RESET),
    .pin10(1'b0), .pin11(_74299_1_pin11), .pin12(CLK), .pin13(D1_2), .pin14(D3_2), .pin15(D5_2),
    .pin16(D7_2), .pin17(SER_OUT), .pin18(1'b0), .pin19(swr_t), .pin20(1'b1));  // open: pin8
  _74161 _74161_1 (
    .pin1(count_reset), .pin2(count_clk), .pin3(1'b0), .pin4(1'b0), .pin5(1'b0), .pin6(1'b0), .pin7(1'b1),
    .pin8(1'b0), .pin9(1'b1), .pin10(1'b1), .pin11(_74161_1_pin11), .pin12(_74161_1_pin12),
    .pin13(_74161_1_pin13), .pin14(_74161_1_pin14), .pin16(1'b1));  // open: pin15
  _7442 _7442_1 (
    .pin1(t0), .pin2(t1), .pin3(t2), .pin4(t3), .pin5(t4), .pin6(t5), .pin7(t6), .pin8(1'b0), .pin9(t7),
    .pin10(t8), .pin11(t9), .pin12(_74161_1_pin11), .pin13(_74161_1_pin12), .pin14(_74161_1_pin13),
    .pin15(_74161_1_pin14), .pin16(1'b1));
  // SwitchDT switchdt_1: pin names not known; wires that end beside it: _74299_1_pin11, SER_OUT, SER_IN

  // Other names for the same wires on the sheet: d0_t = D0_2; d1_t = D1_2; d2_t = D2_2; d3_t = D3_2; d4_t = D4_2;
  //   d5_t = D5_2; d6_t = D6_2; d7_t = D7_2; int_clk = CLK; srd = RD; sreset = RESET; swr = WR

  // Notes on the sheet:
  //   RD: default 1
  //   WR: default 1
  //   RESET: default 1
  //   Z80 tri-state Data
endmodule
