// Digital circuit 74165_test_0.dig as structural Verilog
module _74165_test_0 (
  input  clk,
  input  DB0,
  input  DB1,
  input  DB2,
  input  DB3,
  input  DB4,
  input  DB5,
  input  DB6,
  input  DB7,
  input  SER,
  input  CLK_INH,
  input  LD,
  output \output ,
  output inverted_output
);

  _74165 _74165_1 (
    .pin1(LD), .pin2(clk), .pin3(DB4), .pin4(DB5), .pin5(DB6), .pin6(DB7), .pin7(inverted_output),
    .pin8(1'b0), .pin9(\output ), .pin10(SER), .pin11(DB0), .pin12(DB1), .pin13(DB2), .pin14(DB3),
    .pin15(CLK_INH), .pin16(1'b1));
endmodule
