// Digital circuit 74165_test_1.dig as structural Verilog
module _74165_test_1 (
  input  clk,
  input  DB0,
  input  DB1,
  input  DB2,
  input  DB3,
  input  DB4,
  input  DB5,
  input  DB6,
  input  DB7,
  input  DataSerIn,
  input  ClkInh,
  input  LD,
  output DataOut,
  output DataOut_2,
  output CtrOut,
  output CtrOut_2
);

  _74165 _74165_1 (
    .pin1(LD), .pin2(clk), .pin3(DB4), .pin4(DB5), .pin5(DB6), .pin6(DB7), .pin7(DataOut_2), .pin8(1'b0),
    .pin9(DataOut), .pin10(DataSerIn), .pin11(DB0), .pin12(DB1), .pin13(DB2), .pin14(DB3), .pin15(ClkInh),
    .pin16(1'b1));
  // ScopeTrigger scopetrigger_1: pin names not known; wires that end beside it: clk
  _74165 _74165_2 (
    .pin1(LD), .pin2(clk), .pin3(1'b1), .pin4(1'b1), .pin5(1'b1), .pin6(1'b1), .pin7(CtrOut_2), .pin8(1'b0),
    .pin9(CtrOut), .pin10(1'b0), .pin11(1'b1), .pin12(1'b1), .pin13(1'b1), .pin14(1'b1), .pin15(ClkInh),
    .pin16(1'b1));

  // Notes on the sheet:
  //   ClkInh: default 1
  //   LD: default 1
endmodule
