// Digital circuit 74299_test.dig as structural Verilog
module _74299_test (
  input  DI0,
  input  DI1,
  input  DI2,
  input  DI3,
  input  DI4,
  input  DI5,
  input  DI6,
  input  DI7,
  input  clk,
  input  OE,
  input  S0,
  input  DSL,
  input  DSR,
  input  MR,
  input  S1,
  output DO0,
  output DO1,
  output DO2,
  output DO3,
  output DO4,
  output DO5,
  output DO6,
  output DO7,
  output Q7,
  output Q0
);

  _74299 _74299_1 (
    .pin1(S0), .pin2(OE), .pin3(OE), .pin4(DI6), .pin5(DI4), .pin6(DI2), .pin7(DI0), .pin8(Q0), .pin9(MR),
    .pin10(1'b0), .pin11(DSR), .pin12(clk), .pin13(DI1), .pin14(DI3), .pin15(DI5), .pin16(DI7), .pin17(Q7),
    .pin18(DSL), .pin19(S1), .pin20(1'b1));

  assign DO0 = DI0;
  assign DO1 = DI1;
  assign DO2 = DI2;
  assign DO3 = DI3;
  assign DO4 = DI4;
  assign DO5 = DI5;
  assign DO6 = DI6;
  assign DO7 = DI7;

  // Other names for the same wires on the sheet: d0 = DI0; d1 = DI1; d2 = DI2; d3 = DI3; d4 = DI4; d5 = DI5; d6 = DI6;
  //   d7 = DI7

  // Notes on the sheet:
  //   MR: default 1
endmodule
