// Digital circuit 7493_test.dig as structural Verilog
module _7493_test (
  input  clk,
  input  Reset,
  output B,
  output A,
  output C,
  output D
);

  _7493 _7493_1 (
    .pin1(A), .pin2(Reset), .pin3(Reset), .pin5(1'b1), .pin8(C), .pin9(B), .pin10(1'b0), .pin11(D),
    .pin12(A), .pin14(clk));  // open: pin4, pin6, pin7, pin13
  // ScopeTrigger scopetrigger_1: pin names not known; wires that end beside it: clk
endmodule
