// Digital circuit clock_divider.dig as structural Verilog
module clock_divider (
  input  clk,
  output div4,
  output div2
);

  wire _7474_1_pin2, _7474_1_pin8;

  // ScopeTrigger scopetrigger_1: pin names not known; wires that end beside it: clk
  _7474 _7474_1 (
    .pin1(1'b1), .pin2(_7474_1_pin2), .pin3(clk), .pin4(1'b1), .pin5(div2), .pin6(_7474_1_pin2), .pin7(1'b0),
    .pin8(_7474_1_pin8), .pin9(div4), .pin10(1'b1), .pin11(div2), .pin12(_7474_1_pin8), .pin13(1'b1),
    .pin14(1'b1));
endmodule
