// Digital circuit spi_loopback.dig as structural Verilog
module spi_loopback (
  input  LD,
  input  DO0,
  input  DO1,
  input  DO2,
  input  DO3,
  input  DO4,
  input  DO5,
  input  DO6,
  input  DO7,
  input  CLK,
  input  enable,
  output CS,
  output SCK,
  output DI0,
  output DI1,
  output DI2,
  output DI3,
  output DI4,
  output DI5,
  output DI6,
  output DI7
);

  wire _74164_1_pin8, _74165_1_pin10, _74165_3_pin9, _74165_3_pin10, clk_t_t, ld_t;

  and and_1 (clk_t_t, CLK, enable);
  not not_1 (ld_t, LD);
  not not_2 (SCK, clk_t_t);
  // ScopeTrigger scopetrigger_1: pin names not known; wires that end beside it: SCK
  _74165 _74165_1 (
    .pin1(LD), .pin2(clk_t_t), .pin3(1'b1), .pin4(1'b1), .pin5(1'b1), .pin6(1'b0), .pin8(1'b0), .pin9(CS),
    .pin10(_74165_1_pin10), .pin11(1'b1), .pin12(1'b1), .pin13(1'b1), .pin14(1'b1), .pin15(ld_t), .pin16(1'b1));  // open: pin7
  _74165 _74165_2 (
    .pin1(LD), .pin2(clk_t_t), .pin3(1'b0), .pin4(1'b0), .pin5(1'b0), .pin6(1'b1), .pin8(1'b0),
    .pin9(_74165_1_pin10), .pin10(1'b0), .pin11(1'b0), .pin12(1'b0), .pin13(1'b0), .pin14(1'b0),
    .pin15(ld_t), .pin16(1'b1));  // open: pin7
  _74165 _74165_3 (
    .pin1(LD), .pin2(clk_t_t), .pin3(DO5), .pin4(DO6), .pin5(DO7), .pin6(1'b0), .pin8(1'b0),
    .pin9(_74165_3_pin9), .pin10(_74165_3_pin10), .pin11(DO1), .pin12(DO2), .pin13(DO3), .pin14(DO4),
    .pin15(ld_t), .pin16(1'b1));  // open: pin7
  _74165 _74165_4 (
    .pin1(LD), .pin2(clk_t_t), .pin3(1'b0), .pin4(1'b0), .pin5(1'b0), .pin6(DO0), .pin8(1'b0),
    .pin9(_74165_3_pin10), .pin10(1'b0), .pin11(1'b0), .pin12(1'b0), .pin13(1'b0), .pin14(1'b0),
    .pin15(ld_t), .pin16(1'b1));  // open: pin7
  _74164 _74164_1 (
    .pin1(_74165_3_pin9), .pin2(CS), .pin3(DI0), .pin4(DI1), .pin5(DI2), .pin6(DI3), .pin7(1'b0),
    .pin8(_74164_1_pin8), .pin9(LD), .pin10(DI4), .pin11(DI5), .pin12(DI6), .pin13(DI7), .pin14(1'b1));
  and and_2 (_74164_1_pin8, SCK, CS);

  // Other names for the same wires on the sheet: clk_t = SCK

  // Notes on the sheet:
  //   LD: default 1
  //   Counter
  //   Serial Out
  //   Loop back
  //   Serial In
endmodule
