// Digital circuit spi_simplification_1_jk.dig as structural Verilog
module spi_simplification_1_jk (
  input  LD,
  input  D0,
  input  D1,
  input  D2,
  input  D3,
  input  D4,
  input  D5,
  input  D6,
  input  D7,
  input  CLK,
  input  enable,
  output SerOut,
  output CS,
  output SCK
);

  wire _74112_1_pin9, _74112_1_pin10, _74112_1_pin14, _74165_1_pin10, clk_t_t, ld_t, not_3_out;

  and and_1 (clk_t_t, CLK, enable);
  not not_1 (ld_t, LD);
  not not_2 (SCK, clk_t_t);
  // ScopeTrigger scopetrigger_1: pin names not known; wires that end beside it: SCK
  _74165 _74165_1 (
    .pin1(LD), .pin2(clk_t_t), .pin3(1'b1), .pin4(1'b1), .pin5(1'b1), .pin6(1'b0), .pin8(1'b0), .pin9(CS),
    .pin10(_74165_1_pin10), .pin11(1'b1), .pin12(1'b1), .pin13(1'b1), .pin14(1'b1), .pin15(ld_t), .pin16(1'b1));  // open: pin7
  _74112 _74112_1 (
    .pin1(SCK), .pin2(1'b1), .pin3(1'b0), .pin4(LD), .pin5(_74165_1_pin10), .pin8(1'b0),
    .pin9(_74112_1_pin9), .pin10(_74112_1_pin10), .pin11(1'b0), .pin12(1'b0), .pin13(SCK),
    .pin14(_74112_1_pin14), .pin15(1'b1), .pin16(1'b1));  // open: pin6, pin7
  _74165 _74165_2 (
    .pin1(LD), .pin2(clk_t_t), .pin3(D5), .pin4(D6), .pin5(D7), .pin6(1'b0), .pin8(1'b0), .pin9(SerOut),
    .pin10(_74112_1_pin9), .pin11(D1), .pin12(D2), .pin13(D3), .pin14(D4), .pin15(ld_t), .pin16(1'b1));  // open: pin7
  nand nand_1 (_74112_1_pin14, ld_t, not_3_out);
  nand nand_2 (_74112_1_pin10, D0, ld_t);
  not not_3 (not_3_out, D0);

  // Other names for the same wires on the sheet: clk_t = SCK

  // Notes on the sheet:
  //   LD: default 1
  //   enable: default 1
  //   Counter
  //   Serial Out
endmodule
