// Digital circuit spi_simplification_2_74163.dig as structural Verilog
module spi_simplification_2_74163 (
  input  LD,
  input  D0,
  input  D1,
  input  D2,
  input  D3,
  input  D4,
  input  D5,
  input  D6,
  input  D7,
  input  CLK,
  input  enable,
  output SerOut,
  output CS,
  output SCK
);

  wire _74163_1_pin10, _74163_1_pin11, _74163_1_pin14, and_2_out, and_3_out, clk_t_t, cs_t, ld_t, nor_4_out,
       not_3_out, or_1_out;

  and and_1 (clk_t_t, CLK, enable);
  not not_1 (ld_t, LD);
  not not_2 (SCK, clk_t_t);
  // ScopeTrigger scopetrigger_1: pin names not known; wires that end beside it: SCK
  _74163 _74163_1 (
    .pin1(LD), .pin2(clk_t_t), .pin3(1'b0), .pin4(1'b0), .pin5(1'b0), .pin6(1'b0), .pin7(1'b1), .pin8(1'b0),
    .pin9(1'b1), .pin10(_74163_1_pin10), .pin11(_74163_1_pin11), .pin14(_74163_1_pin14), .pin16(1'b1));  // open: pin12, pin13, pin15
  not not_3 (not_3_out, _74163_1_pin11);
  and and_2 (and_2_out, not_3_out, _74163_1_pin14);
  and and_3 (and_3_out, _74163_1_pin14, _74163_1_pin11);
  or or_1 (or_1_out, ld_t, and_3_out);
  nor nor_1 (cs_t, and_2_out, CS);
  nor nor_2 (CS, cs_t, or_1_out);
  nor nor_3 (_74163_1_pin10, and_3_out, nor_4_out);
  nor nor_4 (nor_4_out, _74163_1_pin10, ld_t);
  _74165 _74165_1 (
    .pin1(LD), .pin2(clk_t_t), .pin3(D4), .pin4(D5), .pin5(D6), .pin6(D7), .pin8(1'b0), .pin9(SerOut),
    .pin10(1'b0), .pin11(D0), .pin12(D1), .pin13(D2), .pin14(D3), .pin15(cs_t), .pin16(1'b1));  // open: pin7

  // Other names for the same wires on the sheet: clk_t = SCK

  // Notes on the sheet:
  //   LD: default 1
  //   enable: default 1
  //   Counter
  //   Serial Out
endmodule
